# Fritzing sketch Untitled Sketch (saved by Fritzing 0.9.3b)
breadboards: 1

parts:
  U1 = NodeMCU V1.0
  J1 = Basic Servo
  hc-sr1 = hc-sr04
  M1 = fc-51 [package=THT]

nets:
  N1: U1.D0, J1.pulse
  N2: U1.D1, hc-sr1.Echo
  N3: U1.D2, M1.pin1
  GND: U1.GND, J1.gnd, hc-sr1.GND, M1.pin2
  VCC: J1.vcc, hc-sr1.VCC, M1.pin3

custom parts:
  NodeMCU V1.0: ESP8266 based NodeMCU
